# Fritzing sketch ESP32 Diagram Final (saved by Fritzing 0.9.3b)

parts:
  M5 = DOIT Esp32 DevKit v1 (30 pins long, 11 pins width) [part_number=ESP32S-PIN30]
  HC-SR04_Sensor_3 = HC-SR04 Ultrasonic Distance Sensor [part_number="US 2"]
  HC-SR04_Sensor_4 = HC-SR04 Ultrasonic Distance Sensor [part_number="US 1"]
  S2 = H-Bridge with L298N
  M6 = DC Motor
  M7 = DC Motor
  J3 = Basic Servo

nets:
  VCC: M5.3V3, HC-SR04_Sensor_3.VCC, HC-SR04_Sensor_4.VCC
  GND: M5.GND, HC-SR04_Sensor_3.GND, HC-SR04_Sensor_4.GND, S2.GND, J3.gnd
  N1: M5.D4, HC-SR04_Sensor_4.ECHO
  N2: M5.RX2, HC-SR04_Sensor_3.ECHO
  N3: M5.TX2, HC-SR04_Sensor_3.TRIG
  N4: M5.D5, HC-SR04_Sensor_4.TRIG
  N5: M5.D18, J3.pulse
  N6: M5.D19, S2.IN4
  N7: M5.D21, S2.IN3
  N8: M5.D22, S2.IN2
  N9: M5.D23, S2.IN1
  VIN: M5.VIN, J3.vcc
  N10: S2.M1-01, M7.pin_1
  N11: S2.M1-02, M7.pin_2
  N12: S2.M2-01, S2.ENB-5V, M6.pin_2
  N13: S2.M2-02, M6.pin_1

notes:
  Connect to 12 v Battery

custom parts:
  DOIT Esp32 DevKit v1 (30 pins long, 11 pins width): The DOIT Esp32 DevKit v1 is one of the development board created by DOIT to evaluate the ESP-WROOM-32 module. It is based on the ESP32 microcontroller that boasts Wifi, Bluetooth, Ethernet and Low Power support all in a single chip. (vanepp) made breadboard work, adjusted pin numbering and labels and reduced size of schematic and cleaned up pcb. This chip is 30pins long (2 x15) and 11 pins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
  H-Bridge with L298N: h-bridge
